# Fritzing sketch Airok (saved by Fritzing 0.9.3b)
breadboards: 1
perfboards: 1

parts:
  Part1 = Arduino Nano (Rev3.0) (ICSP)
  8-12V = Power plug
  LED1 = LED - 5mm [color="Red (633nm)" package="5 mm [THT]"]
  R1 = Resistor [tolerance=±10% resistance=330 package=THT]
  TTP223 = mystery part, 3 pins [chip_label=TTP223]
  BMP180 = Barometric Pressure Sensor - BMP180 Breakout (GY-68)
  R2 = Resistor [tolerance=±5% resistance=10k package=THT]
  R3 = Resistor [tolerance=±5% resistance=10k package=THT]
  Oled_Display = mystery part, 4 pins [chip_label="Oled Disp"]
  DHT11 = DHT11 Humitidy and Temperature Sensor
  R4 = Resistor [tolerance=±5% resistance=10k package=THT]
  U1 = ESP8266 WiFi Module [part_number=ESP8266]
  5V_Stabilizer = mystery part, 4 pins [chip_label="5V Stabilizer"]
  TGS4161 = mystery part, 5 pins [chip_label=TGS4161]
  U2 = mystery part, 3 pins [chip_label=3.3V]
  C1 = Electrolytic Capacitor [capacitance=100µF package="100 mil [THT, electrolytic]"]
  C2 = Electrolytic Capacitor [capacitance=100µF package="100 mil [THT, electrolytic]"]

nets:
  GND: Part1.GND, 8-12V.GND, LED1.cathode, TTP223.pin1, BMP180.GND, Oled_Display.pin1, DHT11.GND, U1.GND, 5V_Stabilizer.pin1, 5V_Stabilizer.pin4, TGS4161.pin4, U2.pin1, C2.-
  N1: Part1.D2, DHT11.DATA, R4.Pin_1
  N2: Part1.D3, TTP223.pin2
  N3: Part1.D6, U1.RXD
  N4: Part1.D7, U1.TXD
  N5: Part1.D12/MISO, R1.Pin_0
  VIN: Part1.VIN, 8-12V.VCC, 5V_Stabilizer.pin3, U2.pin3, C1.+
  N6: Part1.A5, BMP180.SCL, R2.Pin_0, Oled_Display.pin3
  N7: Part1.A4, BMP180.SDA, R3.Pin_0, Oled_Display.pin4
  N8: Part1.A0, TGS4161.pin2, TGS4161.pin3
  N9: LED1.anode, R1.Pin_1
  N10: TTP223.pin3, DHT11.VDD, R4.Pin_0, 5V_Stabilizer.pin2, TGS4161.pin1
  N11: BMP180.VCC, R2.Pin_1, R3.Pin_1, Oled_Display.pin2, U1.CH_PD
  N12: U2.pin2, C2.+

custom parts:
  DHT11 Humitidy and Temperature Sensor: DHT11 Humidity and Temperature Sensor
